// Logisim project MINI RAM.circ as structural Verilog: 10 circuits, main circuit main
module main (
  input  in_1,
  input  in_2,
  input  in_3,
  input  in_4,
  input  CLK,
  input  in_6,
  input  in_7,
  input  in_8,
  output out_9,
  output out_10,
  output out_11,
  output out_12,
  output out_13,
  output out_14,
  output out_15,
  output out_16,
  output out_17,
  output out_18,
  output out_19,
  output out_20,
  output out_21,
  output out_22,
  output out_23,
  output out_24,
  output out_25,
  output out_26,
  output out_27,
  output out_28
);

  wire address_register_1_out_4, address_register_1_out_5, data_register_1_out_15, data_register_1_out_16,
       data_register_1_out_17, data_register_1_out_18, merger_1_out_17, merger_1_out_18, merger_1_out_19,
       merger_1_out_20, n00_1_out_3, n01_1_out_3, n10_1_out_3, n11_1_out_3, nibble_1_out_12, nibble_1_out_13,
       nibble_1_out_14, nibble_1_out_15, nibble_2_out_12, nibble_2_out_13, nibble_2_out_14, nibble_2_out_15,
       nibble_3_out_12, nibble_3_out_13, nibble_3_out_14, nibble_3_out_15, nibble_4_out_12, nibble_4_out_13,
       nibble_4_out_14, nibble_4_out_15, r_w_register_1_out_3;

  R_W_REGISTER r_w_register_1 (.in_1(CLK), .in_2(in_6), .out_3(r_w_register_1_out_3));
  _11 u_11_1 (.in_1(address_register_1_out_4), .in_2(address_register_1_out_5), .out_3(n11_1_out_3));
  _10 u_10_1 (.in_1(address_register_1_out_4), .in_2(address_register_1_out_5), .out_3(n10_1_out_3));
  _01 u_01_1 (.in_1(address_register_1_out_4), .in_2(address_register_1_out_5), .out_3(n01_1_out_3));
  ADDRESS_REGISTER address_register_1 (
    .in_1(in_7), .in_2(CLK), .in_3(in_8), .out_4(address_register_1_out_4), .out_5(address_register_1_out_5));
  _00 u_00_1 (.in_1(address_register_1_out_4), .in_2(address_register_1_out_5), .out_3(n00_1_out_3));
  DATA_REGISTER data_register_1 (
    .in_1(merger_1_out_17), .in_2(merger_1_out_18), .in_3(merger_1_out_19), .in_4(merger_1_out_20),
    .in_6(in_1), .in_7(in_2), .in_8(in_3), .in_9(in_4), .in_10(CLK), .out_11(out_13), .out_12(out_14),
    .out_13(out_15), .out_14(out_16), .out_15(data_register_1_out_15), .out_16(data_register_1_out_16),
    .out_17(data_register_1_out_17), .out_18(data_register_1_out_18), .in_5(r_w_register_1_out_3));
  MERGER merger_1 (
    .in_1(nibble_1_out_12), .in_2(nibble_1_out_13), .in_3(nibble_1_out_14), .in_4(nibble_1_out_15),
    .in_5(nibble_2_out_12), .in_6(nibble_2_out_13), .in_7(nibble_2_out_14), .in_8(nibble_2_out_15),
    .in_9(nibble_3_out_12), .in_10(nibble_3_out_13), .in_11(nibble_3_out_14), .in_12(nibble_3_out_15),
    .in_13(nibble_4_out_12), .in_14(nibble_4_out_13), .in_15(nibble_4_out_14), .in_16(nibble_4_out_15),
    .out_17(merger_1_out_17), .out_18(merger_1_out_18), .out_19(merger_1_out_19), .out_20(merger_1_out_20));
  NIBBLE nibble_1 (
    .in_4(data_register_1_out_15), .in_5(data_register_1_out_16), .in_6(data_register_1_out_17),
    .in_7(data_register_1_out_18), .out_12(nibble_1_out_12), .out_13(nibble_1_out_13),
    .out_14(nibble_1_out_14), .out_15(nibble_1_out_15), .WRITE(r_w_register_1_out_3), .in_2(n11_1_out_3),
    .in_3(CLK), .out_8(out_9), .out_9(out_10), .out_10(out_11), .out_11(out_12));
  NIBBLE nibble_2 (
    .in_4(data_register_1_out_15), .in_5(data_register_1_out_16), .in_6(data_register_1_out_17),
    .in_7(data_register_1_out_18), .out_12(nibble_2_out_12), .out_13(nibble_2_out_13),
    .out_14(nibble_2_out_14), .out_15(nibble_2_out_15), .WRITE(r_w_register_1_out_3), .in_2(n10_1_out_3),
    .in_3(CLK), .out_8(out_17), .out_9(out_18), .out_10(out_19), .out_11(out_20));
  NIBBLE nibble_3 (
    .in_4(data_register_1_out_15), .in_5(data_register_1_out_16), .in_6(data_register_1_out_17),
    .in_7(data_register_1_out_18), .out_12(nibble_3_out_12), .out_13(nibble_3_out_13),
    .out_14(nibble_3_out_14), .out_15(nibble_3_out_15), .WRITE(r_w_register_1_out_3), .in_2(n01_1_out_3),
    .in_3(CLK), .out_8(out_21), .out_9(out_22), .out_10(out_23), .out_11(out_24));
  NIBBLE nibble_4 (
    .in_4(data_register_1_out_15), .in_5(data_register_1_out_16), .in_6(data_register_1_out_17),
    .in_7(data_register_1_out_18), .out_12(nibble_4_out_12), .out_13(nibble_4_out_13),
    .out_14(nibble_4_out_14), .out_15(nibble_4_out_15), .WRITE(r_w_register_1_out_3), .in_2(n00_1_out_3),
    .in_3(CLK), .out_8(out_25), .out_9(out_26), .out_10(out_27), .out_11(out_28));

  // Notes on the sheet:
  //   INSTRUCTIONS
  //   TO START:
  //   -Set CLK to 1
  //   TO WRITE:
  //   -Set R/W to 1
  //   -Set data input on
  //   Data Register
  //   to location
  //   TO RE-WRITE:
  //   -Set R/W to 1
  //   -Set data input on
  //   Data Register
  //   to location
  //   -Click CLK 4 times
  //   TO READ:
  //   -Set R/W to 0
  //   to location
  //   -Click CLK 4 times
  //   -Set Address Register
  //   -Click CLK 2 times
  //   -Set Address Register
  //   -Set Address Register
  //   January 31 2015
  //   DANIEL LUTES
  //   # 260609221
endmodule

module DATA_REGISTER (
  input  in_1,
  input  in_2,
  input  in_3,
  input  in_4,
  input  in_5,
  input  in_6,
  input  in_7,
  input  in_8,
  input  in_9,
  input  in_10,
  output out_11,
  output out_12,
  output out_13,
  output out_14,
  output out_15,
  output out_16,
  output out_17,
  output out_18
);

  wire and_1_out, not_1_out;

  and and_1 (and_1_out, not_1_out, in_10);
  D_Flip_Flop d_ff_1 (.clk(and_1_out), .D(in_1), .Q(out_11));  // open: Qn, preset, en, reset
  D_Flip_Flop d_ff_2 (.clk(and_1_out), .D(in_2), .Q(out_12));  // open: Qn, preset, en, reset
  D_Flip_Flop d_ff_3 (.clk(and_1_out), .D(in_3), .Q(out_13));  // open: Qn, preset, en, reset
  D_Flip_Flop d_ff_4 (.clk(and_1_out), .D(in_4), .Q(out_14));  // open: Qn, preset, en, reset
  D_Flip_Flop d_ff_5 (.clk(in_10), .D(in_6), .Q(out_15));  // open: Qn, preset, en, reset
  D_Flip_Flop d_ff_6 (.clk(in_10), .D(in_7), .Q(out_16));  // open: Qn, preset, en, reset
  D_Flip_Flop d_ff_7 (.clk(in_10), .D(in_8), .Q(out_17));  // open: Qn, preset, en, reset
  D_Flip_Flop d_ff_8 (.clk(in_10), .D(in_9), .Q(out_18));  // open: Qn, preset, en, reset
  not not_1 (not_1_out, in_5);
endmodule

module R_W_REGISTER (
  input  in_1,
  input  in_2,
  output out_3
);

  D_Flip_Flop d_ff_1 (.clk(in_1), .D(in_2), .Q(out_3));  // open: Qn, preset, en, reset
endmodule

module ADDRESS_REGISTER (
  input  in_1,
  input  in_2,
  input  in_3,
  output out_4,
  output out_5
);

  D_Flip_Flop d_ff_1 (.clk(in_2), .D(in_1), .Q(out_4));  // open: Qn, preset, en, reset
  D_Flip_Flop d_ff_2 (.clk(in_2), .D(in_3), .Q(out_5));  // open: Qn, preset, en, reset
endmodule

module _00 (
  input  in_1,
  input  in_2,
  output out_3
);

  wire not_1_out, not_2_out;

  not not_1 (not_1_out, in_1);
  not not_2 (not_2_out, in_2);
  and and_1 (out_3, not_1_out, not_2_out);
endmodule

module _01 (
  input  in_1,
  input  in_2,
  output out_3
);

  wire not_1_out;

  not not_1 (not_1_out, in_1);
  and and_1 (out_3, not_1_out, in_2);
endmodule

module _10 (
  input  in_1,
  input  in_2,
  output out_3
);

  wire not_1_out;

  and and_1 (out_3, in_1, not_1_out);
  not not_1 (not_1_out, in_2);
endmodule

module _11 (
  input  in_1,
  input  in_2,
  output out_3
);

  and and_1 (out_3, in_1, in_2);
endmodule

module NIBBLE (
  input  WRITE,
  input  in_2,
  input  in_3,
  input  in_4,
  input  in_5,
  input  in_6,
  input  in_7,
  output out_8,
  output out_9,
  output out_10,
  output out_11,
  output out_12,
  output out_13,
  output out_14,
  output out_15
);

  wire and_1_out, not_1_out;

  and and_1 (and_1_out, WRITE, in_2, in_3);
  not not_1 (not_1_out, WRITE);
  D_Flip_Flop d_ff_1 (.clk(and_1_out), .D(in_4), .Q(out_8));  // open: Qn, preset, en, reset
  D_Flip_Flop d_ff_2 (.clk(and_1_out), .D(in_5), .Q(out_9));  // open: Qn, preset, en, reset
  D_Flip_Flop d_ff_3 (.clk(and_1_out), .D(in_6), .Q(out_10));  // open: Qn, preset, en, reset
  D_Flip_Flop d_ff_4 (.clk(and_1_out), .D(in_7), .Q(out_11));  // open: Qn, preset, en, reset
  and and_2 (out_12, out_8, in_2, not_1_out);
  and and_3 (out_13, out_9, in_2, not_1_out);
  and and_4 (out_14, out_10, in_2, not_1_out);
  and and_5 (out_15, out_11, in_2, not_1_out);
endmodule

module MERGER (
  input  in_1,
  input  in_2,
  input  in_3,
  input  in_4,
  input  in_5,
  input  in_6,
  input  in_7,
  input  in_8,
  input  in_9,
  input  in_10,
  input  in_11,
  input  in_12,
  input  in_13,
  input  in_14,
  input  in_15,
  input  in_16,
  output out_17,
  output out_18,
  output out_19,
  output out_20
);

  or or_1 (out_17, in_1, in_5, in_9, in_13);
  or or_2 (out_18, in_2, in_6, in_10, in_14);
  or or_3 (out_19, in_3, in_7, in_11, in_15);
  or or_4 (out_20, in_4, in_8, in_12, in_16);
endmodule
