// Logisim project 3-Bit Adder.circ as structural Verilog: 8 circuits, main circuit main
module main (
  input  CLK,
  input  in_2,
  input  in_3,
  input  in_4,
  input  in_5,
  input  in_6,
  input  in_7,
  output out_8,
  output out_9,
  output out_10,
  output out_11
);

  wire left_register_1_out_5, left_register_1_out_6, left_register_1_out_7, n3_bit_adder_1_out_7,
       n3_bit_adder_1_out_8, n3_bit_adder_1_out_9, n3_bit_adder_1_out_10, right_register_1_out_5,
       right_register_1_out_6, right_register_1_out_7;

  Left_Register left_register_1 (
    .in_1(in_2), .in_2(in_3), .in_3(in_4), .out_5(left_register_1_out_5), .out_6(left_register_1_out_6),
    .out_7(left_register_1_out_7), .in_4(CLK));
  _3_Bit_Adder u_3_bit_adder_1 (
    .out_7(n3_bit_adder_1_out_7), .in_1(left_register_1_out_5), .in_2(right_register_1_out_5),
    .in_3(left_register_1_out_6), .in_4(right_register_1_out_6), .in_5(left_register_1_out_7),
    .in_6(right_register_1_out_7), .out_10(n3_bit_adder_1_out_10), .out_8(n3_bit_adder_1_out_8),
    .out_9(n3_bit_adder_1_out_9));
  A_Register a_register_1 (
    .in_1(n3_bit_adder_1_out_10), .in_2(n3_bit_adder_1_out_8), .in_3(n3_bit_adder_1_out_9), .out_5(out_9),
    .out_6(out_10), .out_7(out_11), .in_4(CLK));
  Overflow_Register overflow_register_1 (.in_1(CLK), .in_2(n3_bit_adder_1_out_7), .out_3(out_8));
  Right_Register right_register_1 (
    .in_1(in_5), .in_2(in_6), .in_3(in_7), .out_5(right_register_1_out_5), .out_6(right_register_1_out_6),
    .out_7(right_register_1_out_7), .in_4(CLK));

  // Notes on the sheet:
  //   Febuary 12 2015
  //   Daniel Lutes
  //   # 260609221
endmodule

module Left_Register (
  input  in_1,
  input  in_2,
  input  in_3,
  input  in_4,
  output out_5,
  output out_6,
  output out_7
);

  D_Flip_Flop d_ff_1 (.clk(in_4), .D(in_1), .Q(out_5));  // open: Qn, preset, en, reset
  D_Flip_Flop d_ff_2 (.clk(in_4), .D(in_2), .Q(out_6));  // open: Qn, preset, en, reset
  D_Flip_Flop d_ff_3 (.clk(in_4), .D(in_3), .Q(out_7));  // open: Qn, preset, en, reset
endmodule

module Right_Register (
  input  in_1,
  input  in_2,
  input  in_3,
  input  in_4,
  output out_5,
  output out_6,
  output out_7
);

  D_Flip_Flop d_ff_1 (.clk(in_4), .D(in_1), .Q(out_5));  // open: Qn, preset, en, reset
  D_Flip_Flop d_ff_2 (.clk(in_4), .D(in_2), .Q(out_6));  // open: Qn, preset, en, reset
  D_Flip_Flop d_ff_3 (.clk(in_4), .D(in_3), .Q(out_7));  // open: Qn, preset, en, reset
endmodule

module Half_Adder (
  input  in_1,
  input  in_2,
  output out_3,
  output out_4
);

  and and_1 (out_3, in_1, in_2);
  xor xor_1 (out_4, in_1, in_2);
endmodule

module Full_Adder (
  input  C,
  input  A__B,
  input  in_3,
  output out_4,
  output out_5
);

  wire half_adder_1_out_3, half_adder_1_out_4, half_adder_2_out_3;

  Half_Adder half_adder_1 (.in_1(A__B), .in_2(in_3), .out_3(half_adder_1_out_3), .out_4(half_adder_1_out_4));
  Half_Adder half_adder_2 (.in_1(C), .in_2(half_adder_1_out_4), .out_3(half_adder_2_out_3), .out_4(out_4));
  or or_1 (out_5, half_adder_2_out_3, half_adder_1_out_3);
endmodule

module _3_Bit_Adder (
  input  in_1,
  input  in_2,
  input  in_3,
  input  in_4,
  input  in_5,
  input  in_6,
  output out_7,
  output out_8,
  output out_9,
  output out_10
);

  wire full_adder_2_out_5, half_adder_1_out_3;

  Full_Adder full_adder_1 (.C(full_adder_2_out_5), .A__B(in_1), .in_3(in_2), .out_4(out_10), .out_5(out_7));
  Half_Adder half_adder_1 (.in_1(in_5), .in_2(in_6), .out_3(half_adder_1_out_3), .out_4(out_9));
  Full_Adder full_adder_2 (.C(half_adder_1_out_3), .A__B(in_3), .in_3(in_4), .out_4(out_8), .out_5(full_adder_2_out_5));
endmodule

module A_Register (
  input  in_1,
  input  in_2,
  input  in_3,
  input  in_4,
  output out_5,
  output out_6,
  output out_7
);

  D_Flip_Flop d_ff_1 (.clk(in_4), .D(in_1), .Q(out_5));  // open: Qn, preset, en, reset
  D_Flip_Flop d_ff_2 (.clk(in_4), .D(in_2), .Q(out_6));  // open: Qn, preset, en, reset
  D_Flip_Flop d_ff_3 (.clk(in_4), .D(in_3), .Q(out_7));  // open: Qn, preset, en, reset
endmodule

module Overflow_Register (
  input  in_1,
  input  in_2,
  output out_3
);

  D_Flip_Flop d_ff_1 (.clk(in_1), .D(in_2), .Q(out_3));  // open: Qn, preset, en, reset
endmodule
