// Logisim project RAM.circ as structural Verilog: 7 circuits, main circuit RAM
module RAM (
  input  in_1,
  input  in_2,
  input  in_3,
  input  in_4,
  input  in_5,
  input  in_6,
  input  in_7,
  input  in_8,
  input  in_9,
  input  in_10,
  input  in_11,
  input  in_12,
  input  in_13,
  input  in_14,
  output out_15,
  output out_16,
  output out_17,
  output out_18,
  output out_19,
  output out_20,
  output out_21,
  output out_22
);

  wire address_register_1_out_6, address_register_1_out_7, address_register_1_out_8,
       address_register_1_out_9, data_register_1_out_27, data_register_1_out_28, data_register_1_out_29,
       data_register_1_out_30, data_register_1_out_32, data_register_1_out_33, data_register_1_out_34,
       merger_1_out_129, merger_1_out_130, merger_1_out_131, merger_1_out_132, merger_1_out_133,
       merger_1_out_134, merger_1_out_135, merger_1_out_136, n4bit_decoder_1__0, n4bit_decoder_1__1,
       n4bit_decoder_1__2, n4bit_decoder_1__3, n4bit_decoder_1__4, n4bit_decoder_1__5, n4bit_decoder_1__6,
       n4bit_decoder_1__7, n4bit_decoder_1__8, n4bit_decoder_1__9, n4bit_decoder_1__10, n4bit_decoder_1__11,
       n4bit_decoder_1__12, n4bit_decoder_1__13, n4bit_decoder_1__14, n4bit_decoder_1__15,
       n8bit_register_1_out_12, n8bit_register_1_out_13, n8bit_register_1_out_14, n8bit_register_1_out_15,
       n8bit_register_1_out_16, n8bit_register_1_out_17, n8bit_register_1_out_18, n8bit_register_1_out_19,
       n8bit_register_2_out_12, n8bit_register_2_out_13, n8bit_register_2_out_14, n8bit_register_2_out_15,
       n8bit_register_2_out_16, n8bit_register_2_out_17, n8bit_register_2_out_18, n8bit_register_2_out_19,
       n8bit_register_3_out_12, n8bit_register_3_out_13, n8bit_register_3_out_14, n8bit_register_3_out_15,
       n8bit_register_3_out_16, n8bit_register_3_out_17, n8bit_register_3_out_18, n8bit_register_3_out_19,
       n8bit_register_4_out_12, n8bit_register_4_out_13, n8bit_register_4_out_14, n8bit_register_4_out_15,
       n8bit_register_4_out_16, n8bit_register_4_out_17, n8bit_register_4_out_18, n8bit_register_4_out_19,
       n8bit_register_5_out_12, n8bit_register_5_out_13, n8bit_register_5_out_14, n8bit_register_5_out_15,
       n8bit_register_5_out_16, n8bit_register_5_out_17, n8bit_register_5_out_18, n8bit_register_5_out_19,
       n8bit_register_6_out_12, n8bit_register_6_out_13, n8bit_register_6_out_14, n8bit_register_6_out_15,
       n8bit_register_6_out_16, n8bit_register_6_out_17, n8bit_register_6_out_18, n8bit_register_6_out_19,
       n8bit_register_7_out_12, n8bit_register_7_out_13, n8bit_register_7_out_14, n8bit_register_7_out_15,
       n8bit_register_7_out_16, n8bit_register_7_out_17, n8bit_register_7_out_18, n8bit_register_7_out_19,
       n8bit_register_8_out_12, n8bit_register_8_out_13, n8bit_register_8_out_14, n8bit_register_8_out_15,
       n8bit_register_8_out_16, n8bit_register_8_out_17, n8bit_register_8_out_18, n8bit_register_8_out_19,
       n8bit_register_9_out_12, n8bit_register_9_out_13, n8bit_register_9_out_14, n8bit_register_9_out_15,
       n8bit_register_9_out_16, n8bit_register_9_out_17, n8bit_register_9_out_18, n8bit_register_9_out_19,
       n8bit_register_10_out_12, n8bit_register_10_out_13, n8bit_register_10_out_14,
       n8bit_register_10_out_15, n8bit_register_10_out_16, n8bit_register_10_out_17,
       n8bit_register_10_out_18, n8bit_register_10_out_19, n8bit_register_11_out_12,
       n8bit_register_11_out_13, n8bit_register_11_out_14, n8bit_register_11_out_15,
       n8bit_register_11_out_16, n8bit_register_11_out_17, n8bit_register_11_out_18,
       n8bit_register_11_out_19, n8bit_register_12_out_12, n8bit_register_12_out_13,
       n8bit_register_12_out_14, n8bit_register_12_out_15, n8bit_register_12_out_16,
       n8bit_register_12_out_17, n8bit_register_12_out_18, n8bit_register_12_out_19,
       n8bit_register_13_out_12, n8bit_register_13_out_13, n8bit_register_13_out_14,
       n8bit_register_13_out_15, n8bit_register_13_out_16, n8bit_register_13_out_17,
       n8bit_register_13_out_18, n8bit_register_13_out_19, n8bit_register_14_out_12,
       n8bit_register_14_out_13, n8bit_register_14_out_14, n8bit_register_14_out_15,
       n8bit_register_14_out_16, n8bit_register_14_out_17, n8bit_register_14_out_18,
       n8bit_register_14_out_19, n8bit_register_15_out_12, n8bit_register_15_out_13,
       n8bit_register_15_out_14, n8bit_register_15_out_15, n8bit_register_15_out_16,
       n8bit_register_15_out_17, n8bit_register_15_out_18, n8bit_register_15_out_19,
       n8bit_register_16_out_12, n8bit_register_16_out_13, n8bit_register_16_out_14,
       n8bit_register_16_out_15, n8bit_register_16_out_16, n8bit_register_16_out_17,
       n8bit_register_16_out_18, n8bit_register_16_out_19, r_w_register_1_out_3;

  Data_Register data_register_1 (
    .in_1(merger_1_out_129), .in_2(merger_1_out_130), .in_3(merger_1_out_131), .in_4(merger_1_out_132),
    .in_5(merger_1_out_133), .in_6(merger_1_out_134), .in_7(merger_1_out_135), .in_8(merger_1_out_136),
    .in_10(in_1), .in_11(in_2), .in_12(in_3), .in_13(in_4), .in_14(in_5), .in_15(in_6), .in_16(in_7),
    .in_17(in_8), .in_18(in_14), .out_19(out_15), .out_20(out_16), .out_21(out_17), .out_22(out_18),
    .out_23(out_19), .out_24(out_20), .out_25(out_21), .out_26(out_22), .in_9(r_w_register_1_out_3),
    .out_27(data_register_1_out_27), .out_28(data_register_1_out_28), .out_29(data_register_1_out_29),
    .out_30(data_register_1_out_30), .out_32(data_register_1_out_32), .out_33(data_register_1_out_33),
    .out_34(data_register_1_out_34));  // open: out_31
  Address_Register address_register_1 (
    .in_1(in_9), .in_2(in_14), .in_3(in_10), .in_4(in_11), .in_5(in_12), .out_6(address_register_1_out_6),
    .out_7(address_register_1_out_7), .out_8(address_register_1_out_8), .out_9(address_register_1_out_9));
  R_W_Register r_w_register_1 (.in_1(in_14), .in_2(in_13), .out_3(r_w_register_1_out_3));
  _4bit_Decoder u_4bit_decoder_1 (
    ._15(n4bit_decoder_1__15), ._14(n4bit_decoder_1__14), ._13(n4bit_decoder_1__13),
    ._12(n4bit_decoder_1__12), ._11(n4bit_decoder_1__11), ._10(n4bit_decoder_1__10), ._9(n4bit_decoder_1__9),
    ._8(n4bit_decoder_1__8), ._7(n4bit_decoder_1__7), ._6(n4bit_decoder_1__6), ._5(n4bit_decoder_1__5),
    ._4(n4bit_decoder_1__4), ._3(n4bit_decoder_1__3), ._2(n4bit_decoder_1__2), ._1(n4bit_decoder_1__1),
    ._0(n4bit_decoder_1__0), .in_1(address_register_1_out_6), .in_2(address_register_1_out_7),
    .in_3(address_register_1_out_8), .in_4(address_register_1_out_9));
  _8bit_Register u_8bit_register_1 (
    .in_4(data_register_1_out_27), .in_5(data_register_1_out_28), .in_6(data_register_1_out_29),
    .in_7(data_register_1_out_30), .in_8(data_register_1_out_30), .in_9(data_register_1_out_32),
    .in_10(data_register_1_out_33), .in_11(data_register_1_out_34), .out_12(n8bit_register_1_out_12),
    .out_13(n8bit_register_1_out_13), .out_14(n8bit_register_1_out_14), .out_15(n8bit_register_1_out_15),
    .out_16(n8bit_register_1_out_16), .out_17(n8bit_register_1_out_17), .out_18(n8bit_register_1_out_18),
    .out_19(n8bit_register_1_out_19), .in_1(r_w_register_1_out_3), .in_2(in_14), .in_3(n4bit_decoder_1__0));
  _8bit_Register u_8bit_register_2 (
    .in_4(data_register_1_out_27), .in_5(data_register_1_out_28), .in_6(data_register_1_out_29),
    .in_7(data_register_1_out_30), .in_8(data_register_1_out_30), .in_9(data_register_1_out_32),
    .in_10(data_register_1_out_33), .in_11(data_register_1_out_34), .out_12(n8bit_register_2_out_12),
    .out_13(n8bit_register_2_out_13), .out_14(n8bit_register_2_out_14), .out_15(n8bit_register_2_out_15),
    .out_16(n8bit_register_2_out_16), .out_17(n8bit_register_2_out_17), .out_18(n8bit_register_2_out_18),
    .out_19(n8bit_register_2_out_19), .in_1(r_w_register_1_out_3), .in_2(in_14), .in_3(n4bit_decoder_1__1));
  _8bit_Register u_8bit_register_3 (
    .in_4(data_register_1_out_27), .in_5(data_register_1_out_28), .in_6(data_register_1_out_29),
    .in_7(data_register_1_out_30), .in_8(data_register_1_out_30), .in_9(data_register_1_out_32),
    .in_10(data_register_1_out_33), .in_11(data_register_1_out_34), .out_12(n8bit_register_3_out_12),
    .out_13(n8bit_register_3_out_13), .out_14(n8bit_register_3_out_14), .out_15(n8bit_register_3_out_15),
    .out_16(n8bit_register_3_out_16), .out_17(n8bit_register_3_out_17), .out_18(n8bit_register_3_out_18),
    .out_19(n8bit_register_3_out_19), .in_1(r_w_register_1_out_3), .in_2(in_14), .in_3(n4bit_decoder_1__2));
  _8bit_Register u_8bit_register_4 (
    .in_4(data_register_1_out_27), .in_5(data_register_1_out_28), .in_6(data_register_1_out_29),
    .in_7(data_register_1_out_30), .in_8(data_register_1_out_30), .in_9(data_register_1_out_32),
    .in_10(data_register_1_out_33), .in_11(data_register_1_out_34), .out_12(n8bit_register_4_out_12),
    .out_13(n8bit_register_4_out_13), .out_14(n8bit_register_4_out_14), .out_15(n8bit_register_4_out_15),
    .out_16(n8bit_register_4_out_16), .out_17(n8bit_register_4_out_17), .out_18(n8bit_register_4_out_18),
    .out_19(n8bit_register_4_out_19), .in_1(r_w_register_1_out_3), .in_2(in_14), .in_3(n4bit_decoder_1__3));
  _8bit_Register u_8bit_register_5 (
    .in_4(data_register_1_out_27), .in_5(data_register_1_out_28), .in_6(data_register_1_out_29),
    .in_7(data_register_1_out_30), .in_8(data_register_1_out_30), .in_9(data_register_1_out_32),
    .in_10(data_register_1_out_33), .in_11(data_register_1_out_34), .out_12(n8bit_register_5_out_12),
    .out_13(n8bit_register_5_out_13), .out_14(n8bit_register_5_out_14), .out_15(n8bit_register_5_out_15),
    .out_16(n8bit_register_5_out_16), .out_17(n8bit_register_5_out_17), .out_18(n8bit_register_5_out_18),
    .out_19(n8bit_register_5_out_19), .in_1(r_w_register_1_out_3), .in_2(in_14), .in_3(n4bit_decoder_1__4));
  _8bit_Register u_8bit_register_6 (
    .in_4(data_register_1_out_27), .in_5(data_register_1_out_28), .in_6(data_register_1_out_29),
    .in_7(data_register_1_out_30), .in_8(data_register_1_out_30), .in_9(data_register_1_out_32),
    .in_10(data_register_1_out_33), .in_11(data_register_1_out_34), .out_12(n8bit_register_6_out_12),
    .out_13(n8bit_register_6_out_13), .out_14(n8bit_register_6_out_14), .out_15(n8bit_register_6_out_15),
    .out_16(n8bit_register_6_out_16), .out_17(n8bit_register_6_out_17), .out_18(n8bit_register_6_out_18),
    .out_19(n8bit_register_6_out_19), .in_1(r_w_register_1_out_3), .in_2(in_14), .in_3(n4bit_decoder_1__5));
  _8bit_Register u_8bit_register_7 (
    .in_4(data_register_1_out_27), .in_5(data_register_1_out_28), .in_6(data_register_1_out_29),
    .in_7(data_register_1_out_30), .in_8(data_register_1_out_30), .in_9(data_register_1_out_32),
    .in_10(data_register_1_out_33), .in_11(data_register_1_out_34), .out_12(n8bit_register_7_out_12),
    .out_13(n8bit_register_7_out_13), .out_14(n8bit_register_7_out_14), .out_15(n8bit_register_7_out_15),
    .out_16(n8bit_register_7_out_16), .out_17(n8bit_register_7_out_17), .out_18(n8bit_register_7_out_18),
    .out_19(n8bit_register_7_out_19), .in_1(r_w_register_1_out_3), .in_2(in_14), .in_3(n4bit_decoder_1__6));
  _8bit_Register u_8bit_register_8 (
    .in_4(data_register_1_out_27), .in_5(data_register_1_out_28), .in_6(data_register_1_out_29),
    .in_7(data_register_1_out_30), .in_8(data_register_1_out_30), .in_9(data_register_1_out_32),
    .in_10(data_register_1_out_33), .in_11(data_register_1_out_34), .out_12(n8bit_register_8_out_12),
    .out_13(n8bit_register_8_out_13), .out_14(n8bit_register_8_out_14), .out_15(n8bit_register_8_out_15),
    .out_16(n8bit_register_8_out_16), .out_17(n8bit_register_8_out_17), .out_18(n8bit_register_8_out_18),
    .out_19(n8bit_register_8_out_19), .in_1(r_w_register_1_out_3), .in_2(in_14), .in_3(n4bit_decoder_1__7));
  _8bit_Register u_8bit_register_9 (
    .in_4(data_register_1_out_27), .in_5(data_register_1_out_28), .in_6(data_register_1_out_29),
    .in_7(data_register_1_out_30), .in_8(data_register_1_out_30), .in_9(data_register_1_out_32),
    .in_10(data_register_1_out_33), .in_11(data_register_1_out_34), .out_12(n8bit_register_9_out_12),
    .out_13(n8bit_register_9_out_13), .out_14(n8bit_register_9_out_14), .out_15(n8bit_register_9_out_15),
    .out_16(n8bit_register_9_out_16), .out_17(n8bit_register_9_out_17), .out_18(n8bit_register_9_out_18),
    .out_19(n8bit_register_9_out_19), .in_1(r_w_register_1_out_3), .in_2(in_14), .in_3(n4bit_decoder_1__8));
  _8bit_Register u_8bit_register_10 (
    .in_4(data_register_1_out_27), .in_5(data_register_1_out_28), .in_6(data_register_1_out_29),
    .in_7(data_register_1_out_30), .in_8(data_register_1_out_30), .in_9(data_register_1_out_32),
    .in_10(data_register_1_out_33), .in_11(data_register_1_out_34), .out_12(n8bit_register_10_out_12),
    .out_13(n8bit_register_10_out_13), .out_14(n8bit_register_10_out_14), .out_15(n8bit_register_10_out_15),
    .out_16(n8bit_register_10_out_16), .out_17(n8bit_register_10_out_17), .out_18(n8bit_register_10_out_18),
    .out_19(n8bit_register_10_out_19), .in_1(r_w_register_1_out_3), .in_2(in_14), .in_3(n4bit_decoder_1__9));
  _8bit_Register u_8bit_register_11 (
    .in_4(data_register_1_out_27), .in_5(data_register_1_out_28), .in_6(data_register_1_out_29),
    .in_7(data_register_1_out_30), .in_8(data_register_1_out_30), .in_9(data_register_1_out_32),
    .in_10(data_register_1_out_33), .in_11(data_register_1_out_34), .out_12(n8bit_register_11_out_12),
    .out_13(n8bit_register_11_out_13), .out_14(n8bit_register_11_out_14), .out_15(n8bit_register_11_out_15),
    .out_16(n8bit_register_11_out_16), .out_17(n8bit_register_11_out_17), .out_18(n8bit_register_11_out_18),
    .out_19(n8bit_register_11_out_19), .in_1(r_w_register_1_out_3), .in_2(in_14), .in_3(n4bit_decoder_1__10));
  _8bit_Register u_8bit_register_12 (
    .in_4(data_register_1_out_27), .in_5(data_register_1_out_28), .in_6(data_register_1_out_29),
    .in_7(data_register_1_out_30), .in_8(data_register_1_out_30), .in_9(data_register_1_out_32),
    .in_10(data_register_1_out_33), .in_11(data_register_1_out_34), .out_12(n8bit_register_12_out_12),
    .out_13(n8bit_register_12_out_13), .out_14(n8bit_register_12_out_14), .out_15(n8bit_register_12_out_15),
    .out_16(n8bit_register_12_out_16), .out_17(n8bit_register_12_out_17), .out_18(n8bit_register_12_out_18),
    .out_19(n8bit_register_12_out_19), .in_1(r_w_register_1_out_3), .in_2(in_14), .in_3(n4bit_decoder_1__11));
  _8bit_Register u_8bit_register_13 (
    .in_4(data_register_1_out_27), .in_5(data_register_1_out_28), .in_6(data_register_1_out_29),
    .in_7(data_register_1_out_30), .in_8(data_register_1_out_30), .in_9(data_register_1_out_32),
    .in_10(data_register_1_out_33), .in_11(data_register_1_out_34), .out_12(n8bit_register_13_out_12),
    .out_13(n8bit_register_13_out_13), .out_14(n8bit_register_13_out_14), .out_15(n8bit_register_13_out_15),
    .out_16(n8bit_register_13_out_16), .out_17(n8bit_register_13_out_17), .out_18(n8bit_register_13_out_18),
    .out_19(n8bit_register_13_out_19), .in_1(r_w_register_1_out_3), .in_2(in_14), .in_3(n4bit_decoder_1__12));
  _8bit_Register u_8bit_register_14 (
    .in_4(data_register_1_out_27), .in_5(data_register_1_out_28), .in_6(data_register_1_out_29),
    .in_7(data_register_1_out_30), .in_8(data_register_1_out_30), .in_9(data_register_1_out_32),
    .in_10(data_register_1_out_33), .in_11(data_register_1_out_34), .out_12(n8bit_register_14_out_12),
    .out_13(n8bit_register_14_out_13), .out_14(n8bit_register_14_out_14), .out_15(n8bit_register_14_out_15),
    .out_16(n8bit_register_14_out_16), .out_17(n8bit_register_14_out_17), .out_18(n8bit_register_14_out_18),
    .out_19(n8bit_register_14_out_19), .in_1(r_w_register_1_out_3), .in_2(in_14), .in_3(n4bit_decoder_1__13));
  _8bit_Register u_8bit_register_15 (
    .in_4(data_register_1_out_27), .in_5(data_register_1_out_28), .in_6(data_register_1_out_29),
    .in_7(data_register_1_out_30), .in_8(data_register_1_out_30), .in_9(data_register_1_out_32),
    .in_10(data_register_1_out_33), .in_11(data_register_1_out_34), .out_12(n8bit_register_15_out_12),
    .out_13(n8bit_register_15_out_13), .out_14(n8bit_register_15_out_14), .out_15(n8bit_register_15_out_15),
    .out_16(n8bit_register_15_out_16), .out_17(n8bit_register_15_out_17), .out_18(n8bit_register_15_out_18),
    .out_19(n8bit_register_15_out_19), .in_1(r_w_register_1_out_3), .in_2(in_14), .in_3(n4bit_decoder_1__14));
  _8bit_Register u_8bit_register_16 (
    .in_4(data_register_1_out_27), .in_5(data_register_1_out_28), .in_6(data_register_1_out_29),
    .in_7(data_register_1_out_30), .in_8(data_register_1_out_30), .in_9(data_register_1_out_32),
    .in_10(data_register_1_out_33), .in_11(data_register_1_out_34), .out_12(n8bit_register_16_out_12),
    .out_13(n8bit_register_16_out_13), .out_14(n8bit_register_16_out_14), .out_15(n8bit_register_16_out_15),
    .out_16(n8bit_register_16_out_16), .out_17(n8bit_register_16_out_17), .out_18(n8bit_register_16_out_18),
    .out_19(n8bit_register_16_out_19), .in_1(r_w_register_1_out_3), .in_2(in_14), .in_3(n4bit_decoder_1__15));
  Merger merger_1 (
    .in_1(n8bit_register_16_out_12), .in_2(n8bit_register_16_out_13), .in_3(n8bit_register_16_out_14),
    .in_4(n8bit_register_16_out_15), .in_5(n8bit_register_16_out_16), .in_6(n8bit_register_16_out_17),
    .in_7(n8bit_register_16_out_18), .in_8(n8bit_register_16_out_19), .in_9(n8bit_register_15_out_12),
    .in_10(n8bit_register_15_out_13), .in_11(n8bit_register_15_out_14), .in_12(n8bit_register_15_out_15),
    .in_13(n8bit_register_15_out_16), .in_14(n8bit_register_15_out_17), .in_15(n8bit_register_15_out_18),
    .in_16(n8bit_register_15_out_19), .in_17(n8bit_register_14_out_12), .in_18(n8bit_register_14_out_13),
    .in_19(n8bit_register_14_out_14), .in_20(n8bit_register_14_out_15), .in_21(n8bit_register_14_out_16),
    .in_22(n8bit_register_14_out_17), .in_23(n8bit_register_14_out_18), .in_24(n8bit_register_14_out_19),
    .in_25(n8bit_register_13_out_12), .in_26(n8bit_register_13_out_13), .in_27(n8bit_register_13_out_14),
    .in_28(n8bit_register_13_out_15), .in_29(n8bit_register_13_out_16), .in_30(n8bit_register_13_out_17),
    .in_31(n8bit_register_13_out_18), .in_32(n8bit_register_13_out_19), .in_33(n8bit_register_12_out_12),
    .in_34(n8bit_register_12_out_13), .in_35(n8bit_register_12_out_14), .in_36(n8bit_register_12_out_15),
    .in_37(n8bit_register_12_out_16), .in_38(n8bit_register_12_out_17), .in_39(n8bit_register_12_out_18),
    .in_40(n8bit_register_12_out_19), .in_41(n8bit_register_11_out_12), .in_42(n8bit_register_11_out_13),
    .in_43(n8bit_register_11_out_14), .in_44(n8bit_register_11_out_15), .in_45(n8bit_register_11_out_16),
    .in_46(n8bit_register_11_out_17), .in_47(n8bit_register_11_out_18), .in_48(n8bit_register_11_out_19),
    .in_49(n8bit_register_10_out_12), .in_50(n8bit_register_10_out_13), .in_51(n8bit_register_10_out_14),
    .in_52(n8bit_register_10_out_15), .in_53(n8bit_register_10_out_16), .in_54(n8bit_register_10_out_17),
    .in_55(n8bit_register_10_out_18), .in_56(n8bit_register_10_out_19), .in_57(n8bit_register_9_out_12),
    .in_58(n8bit_register_9_out_13), .in_59(n8bit_register_9_out_14), .in_60(n8bit_register_9_out_15),
    .in_61(n8bit_register_9_out_16), .in_62(n8bit_register_9_out_17), .in_63(n8bit_register_9_out_18),
    .in_64(n8bit_register_9_out_19), .in_65(n8bit_register_8_out_12), .in_66(n8bit_register_8_out_13),
    .in_67(n8bit_register_8_out_14), .in_68(n8bit_register_8_out_15), .in_69(n8bit_register_8_out_16),
    .in_70(n8bit_register_8_out_17), .in_71(n8bit_register_8_out_18), .in_72(n8bit_register_8_out_19),
    .in_73(n8bit_register_7_out_12), .in_74(n8bit_register_7_out_13), .in_75(n8bit_register_7_out_14),
    .in_76(n8bit_register_7_out_15), .in_77(n8bit_register_7_out_16), .in_78(n8bit_register_7_out_17),
    .in_79(n8bit_register_7_out_18), .in_80(n8bit_register_7_out_19), .in_81(n8bit_register_6_out_12),
    .in_82(n8bit_register_6_out_13), .in_83(n8bit_register_6_out_14), .in_84(n8bit_register_6_out_15),
    .in_85(n8bit_register_6_out_16), .in_86(n8bit_register_6_out_17), .in_87(n8bit_register_6_out_18),
    .in_88(n8bit_register_6_out_19), .in_89(n8bit_register_5_out_12), .in_90(n8bit_register_5_out_13),
    .in_91(n8bit_register_5_out_14), .in_92(n8bit_register_5_out_15), .in_93(n8bit_register_5_out_16),
    .in_94(n8bit_register_5_out_17), .in_95(n8bit_register_5_out_18), .in_96(n8bit_register_5_out_19),
    .in_97(n8bit_register_4_out_12), .in_98(n8bit_register_4_out_13), .in_99(n8bit_register_4_out_14),
    .in_100(n8bit_register_4_out_15), .in_101(n8bit_register_4_out_16), .in_102(n8bit_register_4_out_17),
    .in_103(n8bit_register_4_out_18), .in_104(n8bit_register_4_out_19), .in_105(n8bit_register_3_out_12),
    .in_106(n8bit_register_3_out_13), .in_107(n8bit_register_3_out_14), .in_108(n8bit_register_3_out_15),
    .in_109(n8bit_register_3_out_16), .in_110(n8bit_register_3_out_17), .in_111(n8bit_register_3_out_18),
    .in_112(n8bit_register_3_out_19), .in_113(n8bit_register_2_out_12), .in_114(n8bit_register_2_out_13),
    .in_115(n8bit_register_2_out_14), .in_116(n8bit_register_2_out_15), .in_117(n8bit_register_2_out_16),
    .in_118(n8bit_register_2_out_17), .in_119(n8bit_register_2_out_18), .in_120(n8bit_register_2_out_19),
    .in_121(n8bit_register_1_out_12), .in_122(n8bit_register_1_out_13), .in_123(n8bit_register_1_out_14),
    .in_124(n8bit_register_1_out_15), .in_125(n8bit_register_1_out_16), .in_126(n8bit_register_1_out_17),
    .in_127(n8bit_register_1_out_18), .in_128(n8bit_register_1_out_19), .out_129(merger_1_out_129),
    .out_130(merger_1_out_130), .out_131(merger_1_out_131), .out_132(merger_1_out_132),
    .out_133(merger_1_out_133), .out_134(merger_1_out_134), .out_135(merger_1_out_135),
    .out_136(merger_1_out_136));
endmodule

module _8bit_Register (
  input  in_1,
  input  in_2,
  input  in_3,
  input  in_4,
  input  in_5,
  input  in_6,
  input  in_7,
  input  in_8,
  input  in_9,
  input  in_10,
  input  in_11,
  output out_12,
  output out_13,
  output out_14,
  output out_15,
  output out_16,
  output out_17,
  output out_18,
  output out_19
);

  wire and_1_out, d_ff_1_q, d_ff_2_q, d_ff_3_q, d_ff_4_q, d_ff_5_q, d_ff_6_q, d_ff_7_q, d_ff_8_q, not_1_out;

  and and_1 (and_1_out, in_1, in_2, in_3);
  not not_1 (not_1_out, in_1);
  D_Flip_Flop d_ff_1 (.clk(and_1_out), .D(in_4), .Q(d_ff_1_q));  // open: Qn, preset, en, reset
  D_Flip_Flop d_ff_2 (.clk(and_1_out), .D(in_5), .Q(d_ff_2_q));  // open: Qn, preset, en, reset
  D_Flip_Flop d_ff_3 (.clk(and_1_out), .D(in_6), .Q(d_ff_3_q));  // open: Qn, preset, en, reset
  D_Flip_Flop d_ff_4 (.clk(and_1_out), .D(in_7), .Q(d_ff_4_q));  // open: Qn, preset, en, reset
  D_Flip_Flop d_ff_5 (.clk(and_1_out), .D(in_8), .Q(d_ff_5_q));  // open: Qn, preset, en, reset
  D_Flip_Flop d_ff_6 (.clk(and_1_out), .D(in_9), .Q(d_ff_6_q));  // open: Qn, preset, en, reset
  D_Flip_Flop d_ff_7 (.clk(and_1_out), .D(in_10), .Q(d_ff_7_q));  // open: Qn, preset, en, reset
  D_Flip_Flop d_ff_8 (.clk(and_1_out), .D(in_11), .Q(d_ff_8_q));  // open: Qn, preset, en, reset
  and and_2 (out_12, d_ff_1_q, not_1_out);
  and and_3 (out_13, d_ff_2_q, not_1_out);
  and and_4 (out_14, d_ff_3_q, not_1_out);
  and and_5 (out_15, d_ff_4_q, not_1_out);
  and and_6 (out_16, d_ff_5_q, not_1_out);
  and and_7 (out_17, d_ff_6_q, not_1_out);
  and and_8 (out_18, d_ff_7_q, not_1_out);
  and and_9 (out_19, d_ff_8_q, not_1_out);
endmodule

module _4bit_Decoder (
  input  in_1,
  input  in_2,
  input  in_3,
  input  in_4,
  output _15,
  output _14,
  output _13,
  output _12,
  output _11,
  output _10,
  output _9,
  output _8,
  output _7,
  output _6,
  output _5,
  output _4,
  output _3,
  output _2,
  output _1,
  output _0
);

  wire not_1_out, not_2_out, not_3_out, not_4_out;

  not not_1 (not_1_out, in_1);
  not not_2 (not_2_out, in_2);
  not not_3 (not_3_out, in_3);
  not not_4 (not_4_out, in_4);
  and and_1 (_15, in_4, in_3, in_2, in_1);
  and and_2 (_14, in_1, in_2, in_3, not_4_out);
  and and_3 (_13, in_4, in_2, not_3_out, in_1);
  and and_4 (_12, in_2, in_1, not_3_out, not_4_out);
  and and_5 (_11, not_2_out, in_1, in_4, in_3);
  and and_6 (_10, in_1, not_2_out, not_4_out, in_3);
  and and_7 (_9, in_4, not_3_out, in_1, not_2_out);
  and and_8 (_8, in_1, not_2_out, not_3_out, not_4_out);
  and and_9 (_7, not_1_out, in_2, in_3, in_4);
  and and_10 (_6, in_2, in_3, not_4_out, not_1_out);
  and and_11 (_5, not_1_out, not_3_out, in_2, in_4);
  and and_12 (_4, in_2, not_4_out, not_3_out, not_1_out);
  and and_13 (_3, not_1_out, not_2_out, in_3, in_4);
  and and_14 (_2, in_3, not_1_out, not_2_out, not_4_out);
  and and_15 (_1, not_1_out, not_2_out, not_3_out, in_4);
  and and_16 (_0, not_4_out, not_3_out, not_2_out, not_1_out);
endmodule

module Address_Register (
  input  in_1,
  input  in_2,
  input  in_3,
  input  in_4,
  input  in_5,
  output out_6,
  output out_7,
  output out_8,
  output out_9
);

  D_Flip_Flop d_ff_1 (.clk(in_2), .D(in_1), .Q(out_6));  // open: Qn, preset, en, reset
  D_Flip_Flop d_ff_2 (.clk(in_2), .D(in_3), .Q(out_7));  // open: Qn, preset, en, reset
  D_Flip_Flop d_ff_3 (.clk(in_2), .D(in_4), .Q(out_8));  // open: Qn, preset, en, reset
  D_Flip_Flop d_ff_4 (.clk(in_2), .D(in_5), .Q(out_9));  // open: Qn, preset, en, reset
endmodule

module R_W_Register (
  input  in_1,
  input  in_2,
  output out_3
);

  D_Flip_Flop d_ff_1 (.clk(in_1), .D(in_2), .Q(out_3));  // open: Qn, preset, en, reset
endmodule

module Data_Register (
  input  in_1,
  input  in_2,
  input  in_3,
  input  in_4,
  input  in_5,
  input  in_6,
  input  in_7,
  input  in_8,
  input  in_9,
  input  in_10,
  input  in_11,
  input  in_12,
  input  in_13,
  input  in_14,
  input  in_15,
  input  in_16,
  input  in_17,
  input  in_18,
  output out_19,
  output out_20,
  output out_21,
  output out_22,
  output out_23,
  output out_24,
  output out_25,
  output out_26,
  output out_27,
  output out_28,
  output out_29,
  output out_30,
  output out_31,
  output out_32,
  output out_33,
  output out_34
);

  wire and_1_out, not_1_out;

  and and_1 (and_1_out, not_1_out, in_18);
  D_Flip_Flop d_ff_1 (.clk(and_1_out), .D(in_1), .Q(out_19));  // open: Qn, preset, en, reset
  D_Flip_Flop d_ff_2 (.clk(and_1_out), .D(in_2), .Q(out_20));  // open: Qn, preset, en, reset
  D_Flip_Flop d_ff_3 (.clk(and_1_out), .D(in_3), .Q(out_21));  // open: Qn, preset, en, reset
  D_Flip_Flop d_ff_4 (.clk(and_1_out), .D(in_4), .Q(out_22));  // open: Qn, preset, en, reset
  D_Flip_Flop d_ff_5 (.clk(and_1_out), .D(in_5), .Q(out_23));  // open: Qn, preset, en, reset
  D_Flip_Flop d_ff_6 (.clk(and_1_out), .D(in_6), .Q(out_24));  // open: Qn, preset, en, reset
  D_Flip_Flop d_ff_7 (.clk(and_1_out), .D(in_7), .Q(out_25));  // open: Qn, preset, en, reset
  D_Flip_Flop d_ff_8 (.clk(and_1_out), .D(in_8), .Q(out_26));  // open: Qn, preset, en, reset
  D_Flip_Flop d_ff_9 (.clk(in_18), .D(in_10), .Q(out_27));  // open: Qn, preset, en, reset
  D_Flip_Flop d_ff_10 (.clk(in_18), .D(in_11), .Q(out_28));  // open: Qn, preset, en, reset
  D_Flip_Flop d_ff_11 (.clk(in_18), .D(in_12), .Q(out_29));  // open: Qn, preset, en, reset
  D_Flip_Flop d_ff_12 (.clk(in_18), .D(in_13), .Q(out_30));  // open: Qn, preset, en, reset
  D_Flip_Flop d_ff_13 (.clk(in_18), .D(in_14), .Q(out_31));  // open: Qn, preset, en, reset
  D_Flip_Flop d_ff_14 (.clk(in_18), .D(in_15), .Q(out_32));  // open: Qn, preset, en, reset
  D_Flip_Flop d_ff_15 (.clk(in_18), .D(in_16), .Q(out_33));  // open: Qn, preset, en, reset
  D_Flip_Flop d_ff_16 (.clk(in_18), .D(in_17), .Q(out_34));  // open: Qn, preset, en, reset
  not not_1 (not_1_out, in_9);
endmodule

module Merger (
  input  in_1,
  input  in_2,
  input  in_3,
  input  in_4,
  input  in_5,
  input  in_6,
  input  in_7,
  input  in_8,
  input  in_9,
  input  in_10,
  input  in_11,
  input  in_12,
  input  in_13,
  input  in_14,
  input  in_15,
  input  in_16,
  input  in_17,
  input  in_18,
  input  in_19,
  input  in_20,
  input  in_21,
  input  in_22,
  input  in_23,
  input  in_24,
  input  in_25,
  input  in_26,
  input  in_27,
  input  in_28,
  input  in_29,
  input  in_30,
  input  in_31,
  input  in_32,
  input  in_33,
  input  in_34,
  input  in_35,
  input  in_36,
  input  in_37,
  input  in_38,
  input  in_39,
  input  in_40,
  input  in_41,
  input  in_42,
  input  in_43,
  input  in_44,
  input  in_45,
  input  in_46,
  input  in_47,
  input  in_48,
  input  in_49,
  input  in_50,
  input  in_51,
  input  in_52,
  input  in_53,
  input  in_54,
  input  in_55,
  input  in_56,
  input  in_57,
  input  in_58,
  input  in_59,
  input  in_60,
  input  in_61,
  input  in_62,
  input  in_63,
  input  in_64,
  input  in_65,
  input  in_66,
  input  in_67,
  input  in_68,
  input  in_69,
  input  in_70,
  input  in_71,
  input  in_72,
  input  in_73,
  input  in_74,
  input  in_75,
  input  in_76,
  input  in_77,
  input  in_78,
  input  in_79,
  input  in_80,
  input  in_81,
  input  in_82,
  input  in_83,
  input  in_84,
  input  in_85,
  input  in_86,
  input  in_87,
  input  in_88,
  input  in_89,
  input  in_90,
  input  in_91,
  input  in_92,
  input  in_93,
  input  in_94,
  input  in_95,
  input  in_96,
  input  in_97,
  input  in_98,
  input  in_99,
  input  in_100,
  input  in_101,
  input  in_102,
  input  in_103,
  input  in_104,
  input  in_105,
  input  in_106,
  input  in_107,
  input  in_108,
  input  in_109,
  input  in_110,
  input  in_111,
  input  in_112,
  input  in_113,
  input  in_114,
  input  in_115,
  input  in_116,
  input  in_117,
  input  in_118,
  input  in_119,
  input  in_120,
  input  in_121,
  input  in_122,
  input  in_123,
  input  in_124,
  input  in_125,
  input  in_126,
  input  in_127,
  input  in_128,
  output out_129,
  output out_130,
  output out_131,
  output out_132,
  output out_133,
  output out_134,
  output out_135,
  output out_136
);

  wire or_1_out, or_3_out, or_4_out, or_5_out, or_6_out, or_8_out, or_9_out, or_10_out, or_11_out, or_12_out,
       or_14_out, or_15_out, or_16_out, or_18_out, or_19_out, or_20_out, or_21_out, or_22_out, or_24_out,
       or_25_out, or_26_out, or_27_out, or_29_out, or_30_out, or_31_out, or_33_out, or_34_out, or_35_out,
       or_36_out, or_37_out, or_39_out, or_40_out;

  buf or_1 (or_1_out, in_121);  // OR_Gate
  or or_2 (out_129, or_1_out, or_3_out, or_4_out, or_5_out);
  or or_3 (or_3_out, in_113, in_105, in_97, in_89, in_81);
  or or_4 (or_4_out, in_73, in_65, in_57, in_49, in_41);
  or or_5 (or_5_out, in_33, in_25, in_17, in_9, in_1);
  buf or_6 (or_6_out, in_122);  // OR_Gate
  or or_7 (out_130, or_6_out, or_9_out, or_8_out, or_10_out);
  or or_8 (or_8_out, in_74, in_66, in_58, in_50, in_42);
  or or_9 (or_9_out, in_114, in_106, in_98, in_90, in_82);
  or or_10 (or_10_out, in_34, in_26, in_18, in_10, in_2);
  or or_11 (or_11_out, in_115, in_107, in_99, in_91, in_83);
  buf or_12 (or_12_out, in_123);  // OR_Gate
  or or_13 (out_131, or_12_out, or_11_out, or_14_out, or_15_out);
  or or_14 (or_14_out, in_75, in_67, in_59, in_51, in_43);
  or or_15 (or_15_out, in_35, in_27, in_19, in_11, in_3);
  buf or_16 (or_16_out, in_124);  // OR_Gate
  or or_17 (out_132, or_16_out, or_18_out, or_19_out, or_20_out);
  or or_18 (or_18_out, in_116, in_108, in_100, in_92, in_84);
  or or_19 (or_19_out, in_76, in_68, in_60, in_52, in_44);
  or or_20 (or_20_out, in_36, in_28, in_20, in_12, in_4);
  or or_21 (or_21_out, in_117, in_109, in_101, in_93, in_85);
  or or_22 (or_22_out, in_4, in_125);
  or or_23 (out_133, or_22_out, or_21_out, or_24_out, or_25_out);
  or or_24 (or_24_out, in_77, in_69, in_61, in_53, in_45);
  or or_25 (or_25_out, in_37, in_29, in_21, in_13, in_5);
  buf or_26 (or_26_out, in_126);  // OR_Gate
  or or_27 (or_27_out, in_118, in_110, in_102, in_94, in_86);
  or or_28 (out_134, or_26_out, or_27_out, or_30_out, or_29_out);
  or or_29 (or_29_out, in_38, in_30, in_22, in_14, in_6);
  or or_30 (or_30_out, in_78, in_70, in_62, in_54, in_46);
  buf or_31 (or_31_out, in_127);  // OR_Gate
  or or_32 (out_135, or_31_out, or_33_out, or_34_out, or_35_out);
  or or_33 (or_33_out, in_119, in_111, in_103, in_95, in_87);
  or or_34 (or_34_out, in_79, in_71, in_63, in_55, in_47);
  or or_35 (or_35_out, in_39, in_31, in_23, in_15, in_7);
  buf or_36 (or_36_out, in_128);  // OR_Gate
  or or_37 (or_37_out, in_120, in_112, in_104, in_96, in_88);
  or or_38 (out_136, or_36_out, or_37_out, or_39_out, or_40_out);
  or or_39 (or_39_out, in_80, in_72, in_64, in_56, in_48);
  or or_40 (or_40_out, in_40, in_32, in_24, in_16, in_8);
endmodule
