// Logisim project input.circ as structural Verilog
module Input (
  input  in_1,
  input  in_2,
  input  in_3,
  input  in_4,
  input  in_5,
  input  in_6,
  input  in_7,
  input  in_8,
  input  in_9,
  input  in_10,
  input  in_11,
  output out_12,
  output out_13,
  output out_14,
  output out_15
);

  wire and_1_out, not_1_out, or_1_out, or_2_out, or_3_out, or_4_out;

  not not_1 (not_1_out, in_10);
  and and_1 (and_1_out, in_10, not_1_out);
  or or_1 (or_1_out, and_1_out, in_3, in_2);
  D_Flip_Flop d_ff_1 (.clk(in_11), .D(or_1_out), .Q(out_12));  // open: Qn, preset, en, reset
  or or_2 (or_2_out, in_1, in_6, in_5, in_4);
  D_Flip_Flop d_ff_2 (.clk(in_11), .D(or_2_out), .Q(out_13));  // open: Qn, preset, en, reset
  or or_3 (or_3_out, in_1, in_6, in_9, in_8);
  or or_4 (or_4_out, in_3, in_1, in_5, in_9, in_7);
  D_Flip_Flop d_ff_3 (.clk(in_11), .D(or_3_out), .Q(out_14));  // open: Qn, preset, en, reset
  D_Flip_Flop d_ff_4 (.clk(in_11), .D(or_4_out), .Q(out_15));  // open: Qn, preset, en, reset
endmodule
